// Logisim project regfile.circ as structural Verilog: 2 circuits, main circuit main
module main (
  input  [4:0] Read_Register_1,
  input  [4:0] Read_Register_2,
  input  [4:0] Write_Register,
  input  [31:0] Write_Data,
  input  Write_Enable,
  input  Clock,
  output [31:0] s0_Value,
  output [31:0] s1_Value,
  output [31:0] s2_Value,
  output [31:0] ra_Value,
  output [31:0] sp_Value,
  output [31:0] Read_Data_1,
  output [31:0] Read_Data_2
);

  wire a0W, a1W, a2W, a3W, atW, demultiplexer_1_out1, demultiplexer_1_out2, demultiplexer_1_out3,
       demultiplexer_1_out4, demultiplexer_1_out5, demultiplexer_1_out6, demultiplexer_1_out7,
       demultiplexer_1_out8, demultiplexer_1_out9, demultiplexer_1_out10, demultiplexer_1_out11,
       demultiplexer_1_out12, demultiplexer_1_out13, demultiplexer_1_out14, demultiplexer_1_out15,
       demultiplexer_1_out16, demultiplexer_1_out17, demultiplexer_1_out18, demultiplexer_1_out19,
       demultiplexer_1_out20, demultiplexer_1_out21, demultiplexer_1_out22, demultiplexer_1_out23,
       demultiplexer_1_out24, demultiplexer_1_out25, demultiplexer_1_out26, demultiplexer_1_out27,
       demultiplexer_1_out28, demultiplexer_1_out29, demultiplexer_1_out30, demultiplexer_1_out31, fpW, gpW,
       k0W, k1W, raW, s0W, s1W, s2W, s3W, s4W, s5W, s6W, s7W, spW, t0W, t1W, t2W, t3W, t4W, t5W, t6W, t7W,
       t8W, t9W, v0W, v1W;
  wire [31:0] a0_q, a1_q, a2_q, a3_q, at_q, fp_q, gp_q, k0_q, k1_q, multiplexer_1_out, multiplexer_2_out,
       multiplexer_3_out, multiplexer_4_out, multiplexer_5_out, multiplexer_6_out, multiplexer_7_out,
       multiplexer_8_out, multiplexer_9_out, multiplexer_10_out, multiplexer_11_out, multiplexer_12_out,
       multiplexer_13_out, multiplexer_14_out, multiplexer_15_out, multiplexer_16_out, multiplexer_17_out,
       multiplexer_18_out, multiplexer_19_out, multiplexer_20_out, multiplexer_21_out, multiplexer_22_out,
       multiplexer_23_out, multiplexer_24_out, multiplexer_25_out, multiplexer_26_out, multiplexer_27_out,
       multiplexer_28_out, multiplexer_29_out, multiplexer_30_out, multiplexer_31_out, multiplexer_32_out,
       s3_q, s4_q, s5_q, s6_q, s7_q, t0_q, t1_q, t2_q, t3_q, t4_q, t5_q, t6_q, t7_q, t8_q, t9_q, v0_q, v1_q,
       zero_q;

  Demultiplexer #(.select(5)) demultiplexer_1 (
    .out1(demultiplexer_1_out1), .out2(demultiplexer_1_out2), .out3(demultiplexer_1_out3),
    .out4(demultiplexer_1_out4), .out5(demultiplexer_1_out5), .out6(demultiplexer_1_out6),
    .out7(demultiplexer_1_out7), .out8(demultiplexer_1_out8), .out9(demultiplexer_1_out9),
    .out10(demultiplexer_1_out10), .out11(demultiplexer_1_out11), .out12(demultiplexer_1_out12),
    .out13(demultiplexer_1_out13), .out14(demultiplexer_1_out14), .out15(demultiplexer_1_out15),
    .out16(demultiplexer_1_out16), .out17(demultiplexer_1_out17), .out18(demultiplexer_1_out18),
    .out19(demultiplexer_1_out19), .out20(demultiplexer_1_out20), .out21(demultiplexer_1_out21),
    .out22(demultiplexer_1_out22), .out23(demultiplexer_1_out23), .out24(demultiplexer_1_out24),
    .out25(demultiplexer_1_out25), .out26(demultiplexer_1_out26), .out27(demultiplexer_1_out27),
    .out28(demultiplexer_1_out28), .out29(demultiplexer_1_out29), .out30(demultiplexer_1_out30),
    .out31(demultiplexer_1_out31), .in(1'b1), .sel(Write_Register));  // open: out0, en
  not not_1 (atW, demultiplexer_1_out1);
  not not_2 (v0W, demultiplexer_1_out2);
  not not_3 (v1W, demultiplexer_1_out3);
  not not_4 (a0W, demultiplexer_1_out4);
  not not_5 (a1W, demultiplexer_1_out5);
  not not_6 (a2W, demultiplexer_1_out6);
  not not_7 (a3W, demultiplexer_1_out7);
  not not_8 (t0W, demultiplexer_1_out8);
  not not_9 (t1W, demultiplexer_1_out9);
  not not_10 (t2W, demultiplexer_1_out10);
  not not_11 (t3W, demultiplexer_1_out11);
  not not_12 (t4W, demultiplexer_1_out12);
  not not_13 (t5W, demultiplexer_1_out13);
  not not_14 (t6W, demultiplexer_1_out14);
  not not_15 (t7W, demultiplexer_1_out15);
  not not_16 (s0W, demultiplexer_1_out16);
  not not_17 (s1W, demultiplexer_1_out17);
  not not_18 (s2W, demultiplexer_1_out18);
  not not_19 (s3W, demultiplexer_1_out19);
  not not_20 (s4W, demultiplexer_1_out20);
  not not_21 (s5W, demultiplexer_1_out21);
  not not_22 (s6W, demultiplexer_1_out22);
  not not_23 (s7W, demultiplexer_1_out23);
  not not_24 (t8W, demultiplexer_1_out24);
  not not_25 (t9W, demultiplexer_1_out25);
  not not_26 (k0W, demultiplexer_1_out26);
  not not_27 (k1W, demultiplexer_1_out27);
  not not_28 (gpW, demultiplexer_1_out28);
  not not_29 (spW, demultiplexer_1_out29);
  not not_30 (fpW, demultiplexer_1_out30);
  not not_31 (raW, demultiplexer_1_out31);
  Register #(.width(32)) zero (.D(multiplexer_1_out), .Q(zero_q), .clk(Clock));  // open: en, clr
  Multiplexer #(.width(32)) multiplexer_1 (.in0({32{1'b0}}), .out(multiplexer_1_out), .sel(1'b0));  // open: in1, en
  Register #(.width(32)) t0 (.D(multiplexer_2_out), .Q(t0_q), .clk(Clock));  // open: en, clr
  Multiplexer #(.width(32)) multiplexer_2 (
    .in0(Write_Data), .in1(t0_q), .out(multiplexer_2_out), .sel(t0W), .en(Write_Enable));
  Multiplexer #(.width(32)) multiplexer_3 (
    .in0(Write_Data), .in1(s0_Value), .out(multiplexer_3_out), .sel(s0W), .en(Write_Enable));
  Register #(.width(32)) s0 (.D(multiplexer_3_out), .Q(s0_Value), .clk(Clock));  // open: en, clr
  Register #(.width(32)) t8 (.D(multiplexer_4_out), .Q(t8_q), .clk(Clock));  // open: en, clr
  Multiplexer #(.width(32)) multiplexer_4 (
    .in0(Write_Data), .in1(t8_q), .out(multiplexer_4_out), .sel(t8W), .en(Write_Enable));
  Register #(.width(32)) at (.D(multiplexer_5_out), .Q(at_q), .clk(Clock));  // open: en, clr
  Multiplexer #(.width(32)) multiplexer_5 (
    .in0(Write_Data), .in1(at_q), .out(multiplexer_5_out), .sel(atW), .en(Write_Enable));
  Register #(.width(32)) t1 (.D(multiplexer_6_out), .Q(t1_q), .clk(Clock));  // open: en, clr
  Multiplexer #(.width(32)) multiplexer_6 (
    .in0(Write_Data), .in1(t1_q), .out(multiplexer_6_out), .sel(t1W), .en(Write_Enable));
  Multiplexer #(.width(32)) multiplexer_7 (
    .in0(Write_Data), .in1(s1_Value), .out(multiplexer_7_out), .sel(s1W), .en(Write_Enable));
  Register #(.width(32)) s1 (.D(multiplexer_7_out), .Q(s1_Value), .clk(Clock));  // open: en, clr
  Register #(.width(32)) t9 (.D(multiplexer_8_out), .Q(t9_q), .clk(Clock));  // open: en, clr
  Multiplexer #(.width(32)) multiplexer_8 (
    .in0(Write_Data), .in1(t9_q), .out(multiplexer_8_out), .sel(t9W), .en(Write_Enable));
  Multiplexer #(.width(32)) multiplexer_9 (
    .in0(Write_Data), .in1(v0_q), .out(multiplexer_9_out), .sel(v0W), .en(Write_Enable));
  Multiplexer #(.width(32)) multiplexer_10 (
    .in0(Write_Data), .in1(t2_q), .out(multiplexer_10_out), .sel(t2W), .en(Write_Enable));
  Multiplexer #(.width(32)) multiplexer_11 (
    .in0(Write_Data), .in1(s2_Value), .out(multiplexer_11_out), .sel(s2W), .en(Write_Enable));
  Multiplexer #(.width(32)) multiplexer_12 (
    .in0(Write_Data), .in1(k0_q), .out(multiplexer_12_out), .sel(k0W), .en(Write_Enable));
  Register #(.width(32)) v0 (.D(multiplexer_9_out), .Q(v0_q), .clk(Clock));  // open: en, clr
  Register #(.width(32)) t2 (.D(multiplexer_10_out), .Q(t2_q), .clk(Clock));  // open: en, clr
  Register #(.width(32)) s2 (.D(multiplexer_11_out), .Q(s2_Value), .clk(Clock));  // open: en, clr
  Register #(.width(32)) k0 (.D(multiplexer_12_out), .Q(k0_q), .clk(Clock));  // open: en, clr
  Register #(.width(32)) v1 (.D(multiplexer_13_out), .Q(v1_q), .clk(Clock));  // open: en, clr
  Multiplexer #(.width(32)) multiplexer_13 (
    .in0(Write_Data), .in1(v1_q), .out(multiplexer_13_out), .sel(v1W), .en(Write_Enable));
  Register #(.width(32)) t3 (.D(multiplexer_14_out), .Q(t3_q), .clk(Clock));  // open: en, clr
  Multiplexer #(.width(32)) multiplexer_14 (
    .in0(Write_Data), .in1(t3_q), .out(multiplexer_14_out), .sel(t3W), .en(Write_Enable));
  Multiplexer #(.width(32)) multiplexer_15 (
    .in0(Write_Data), .in1(s3_q), .out(multiplexer_15_out), .sel(s3W), .en(Write_Enable));
  Register #(.width(32)) s3 (.D(multiplexer_15_out), .Q(s3_q), .clk(Clock));  // open: en, clr
  Multiplexer #(.width(32)) multiplexer_16 (
    .in0(Write_Data), .in1(k1_q), .out(multiplexer_16_out), .sel(k1W), .en(Write_Enable));
  Register #(.width(32)) k1 (.D(multiplexer_16_out), .Q(k1_q), .clk(Clock));  // open: en, clr
  Multiplexer #(.width(32)) multiplexer_17 (
    .in0(Write_Data), .in1(a0_q), .out(multiplexer_17_out), .sel(a0W), .en(Write_Enable));
  Multiplexer #(.width(32)) multiplexer_18 (
    .in0(Write_Data), .in1(t4_q), .out(multiplexer_18_out), .sel(t4W), .en(Write_Enable));
  Multiplexer #(.width(32)) multiplexer_19 (
    .in0(Write_Data), .in1(s4_q), .out(multiplexer_19_out), .sel(s4W), .en(Write_Enable));
  Multiplexer #(.width(32)) multiplexer_20 (
    .in0(Write_Data), .in1(gp_q), .out(multiplexer_20_out), .sel(gpW), .en(Write_Enable));
  Register #(.width(32)) a0 (.D(multiplexer_17_out), .Q(a0_q), .clk(Clock));  // open: en, clr
  Register #(.width(32)) t4 (.D(multiplexer_18_out), .Q(t4_q), .clk(Clock));  // open: en, clr
  Register #(.width(32)) s4 (.D(multiplexer_19_out), .Q(s4_q), .clk(Clock));  // open: en, clr
  Register #(.width(32)) gp (.D(multiplexer_20_out), .Q(gp_q), .clk(Clock));  // open: en, clr
  Multiplexer #(.width(32)) multiplexer_21 (
    .in0(Write_Data), .in1(a1_q), .out(multiplexer_21_out), .sel(a1W), .en(Write_Enable));
  Multiplexer #(.width(32)) multiplexer_22 (
    .in0(Write_Data), .in1(t5_q), .out(multiplexer_22_out), .sel(t5W), .en(Write_Enable));
  Multiplexer #(.width(32)) multiplexer_23 (
    .in0(Write_Data), .in1(s5_q), .out(multiplexer_23_out), .sel(s5W), .en(Write_Enable));
  Multiplexer #(.width(32)) multiplexer_24 (
    .in0(Write_Data), .in1(sp_Value), .out(multiplexer_24_out), .sel(spW), .en(Write_Enable));
  Register #(.width(32)) a1 (.D(multiplexer_21_out), .Q(a1_q), .clk(Clock));  // open: en, clr
  Register #(.width(32)) t5 (.D(multiplexer_22_out), .Q(t5_q), .clk(Clock));  // open: en, clr
  Register #(.width(32)) s5 (.D(multiplexer_23_out), .Q(s5_q), .clk(Clock));  // open: en, clr
  Register #(.width(32)) sp (.D(multiplexer_24_out), .Q(sp_Value), .clk(Clock));  // open: en, clr
  Register #(.width(32)) a2 (.D(multiplexer_25_out), .Q(a2_q), .clk(Clock));  // open: en, clr
  Multiplexer #(.width(32)) multiplexer_25 (
    .in0(Write_Data), .in1(a2_q), .out(multiplexer_25_out), .sel(a2W), .en(Write_Enable));
  Multiplexer #(.width(32)) multiplexer_26 (
    .in0(Write_Data), .in1(t6_q), .out(multiplexer_26_out), .sel(t6W), .en(Write_Enable));
  Register #(.width(32)) t6 (.D(multiplexer_26_out), .Q(t6_q), .clk(Clock));  // open: en, clr
  Multiplexer #(.width(32)) multiplexer_27 (
    .in0(Write_Data), .in1(s6_q), .out(multiplexer_27_out), .sel(s6W), .en(Write_Enable));
  Register #(.width(32)) s6 (.D(multiplexer_27_out), .Q(s6_q), .clk(Clock));  // open: en, clr
  Multiplexer #(.width(32)) multiplexer_28 (
    .in0(Write_Data), .in1(fp_q), .out(multiplexer_28_out), .sel(fpW), .en(Write_Enable));
  Register #(.width(32)) fp (.D(multiplexer_28_out), .Q(fp_q), .clk(Clock));  // open: en, clr
  Multiplexer #(.width(32)) multiplexer_29 (
    .in0(Write_Data), .in1(a3_q), .out(multiplexer_29_out), .sel(a3W), .en(Write_Enable));
  Multiplexer #(.width(32)) multiplexer_30 (
    .in0(Write_Data), .in1(t7_q), .out(multiplexer_30_out), .sel(t7W), .en(Write_Enable));
  Multiplexer #(.width(32)) multiplexer_31 (
    .in0(Write_Data), .in1(s7_q), .out(multiplexer_31_out), .sel(s7W), .en(Write_Enable));
  Multiplexer #(.width(32)) multiplexer_32 (
    .in0(Write_Data), .in1(ra_Value), .out(multiplexer_32_out), .sel(raW), .en(Write_Enable));
  Register #(.width(32)) a3 (.D(multiplexer_29_out), .Q(a3_q), .clk(Clock));  // open: en, clr
  Register #(.width(32)) t7 (.D(multiplexer_30_out), .Q(t7_q), .clk(Clock));  // open: en, clr
  Register #(.width(32)) s7 (.D(multiplexer_31_out), .Q(s7_q), .clk(Clock));  // open: en, clr
  Register #(.width(32)) ra (.D(multiplexer_32_out), .Q(ra_Value), .clk(Clock));  // open: en, clr
  Multiplexer #(.select(5), .width(32)) multiplexer_33 (
    .in0(zero_q), .in1(at_q), .in2(v0_q), .in3(v1_q), .in4(a0_q), .in5(a1_q), .in6(a2_q), .in7(a3_q),
    .in8(t0_q), .in9(t1_q), .in10(t2_q), .in11(t3_q), .in12(t4_q), .in13(t5_q), .in14(t6_q), .in15(t7_q),
    .in16(s0_Value), .in17(s1_Value), .in18(s2_Value), .in19(s3_q), .in20(s4_q), .in21(s5_q), .in22(s6_q),
    .in23(s7_q), .in24(t8_q), .in25(t9_q), .in26(k0_q), .in27(k1_q), .in28(gp_q), .in29(sp_Value),
    .in30(fp_q), .in31(ra_Value), .out(Read_Data_1), .sel(Read_Register_1));  // open: en
  Multiplexer #(.select(5), .width(32)) multiplexer_34 (
    .in0(zero_q), .in1(at_q), .in2(v0_q), .in3(v1_q), .in4(a0_q), .in5(a1_q), .in6(a2_q), .in7(a3_q),
    .in8(t0_q), .in9(t1_q), .in10(t2_q), .in11(t3_q), .in12(t4_q), .in13(t5_q), .in14(t6_q), .in15(t7_q),
    .in16(s0_Value), .in17(s1_Value), .in18(s2_Value), .in19(s3_q), .in20(s4_q), .in21(s5_q), .in22(s6_q),
    .in23(s7_q), .in24(t8_q), .in25(t9_q), .in26(k0_q), .in27(k1_q), .in28(gp_q), .in29(sp_Value),
    .in30(fp_q), .in31(ra_Value), .out(Read_Data_2), .sel(Read_Register_2));  // open: en

  // Other names for the same wires on the sheet: clk = Clock; read_data1[31:0] = Read_Data_1;
  //   read_data2[31:0] = Read_Data_2; read_reg1[4:0] = Read_Register_1; read_reg2[4:0] = Read_Register_2;
  //   write_en = Write_Enable; write_reg[4:0] = Write_Register

  // Notes on the sheet:
  //   INPUTS to your circuit
  //   DON'T CHANGE THE LOCATIONS OF THE INPUTS AND OUTPUTS!
  //   These are DEBUG/TEST outputs from your circuit.
  //   OUTPUTS from your circuit
endmodule

module regs (
);

  wire [31:0] multiplexer_1_out, multiplexer_2_out, multiplexer_3_out, multiplexer_4_out, multiplexer_5_out,
       multiplexer_6_out, multiplexer_7_out, multiplexer_8_out, multiplexer_9_out, multiplexer_10_out,
       multiplexer_11_out, multiplexer_12_out, multiplexer_13_out, multiplexer_14_out, multiplexer_15_out,
       multiplexer_16_out, multiplexer_17_out, multiplexer_18_out, multiplexer_19_out, multiplexer_20_out,
       multiplexer_21_out, multiplexer_22_out, multiplexer_23_out, multiplexer_24_out, multiplexer_25_out,
       multiplexer_26_out, multiplexer_27_out, multiplexer_28_out, multiplexer_29_out, multiplexer_30_out,
       multiplexer_31_out, multiplexer_32_out;

  Multiplexer #(.width(32)) multiplexer_1 (.out(multiplexer_1_out));  // open: in0, in1, sel, en
  Register #(.width(32)) zero (.D(multiplexer_1_out));  // open: en, Q, clk, clr
  Register #(.width(32)) t0 (.D(multiplexer_2_out));  // open: en, Q, clk, clr
  Multiplexer #(.width(32)) multiplexer_2 (.out(multiplexer_2_out));  // open: in0, in1, sel, en
  Register #(.width(32)) s0 (.D(multiplexer_3_out));  // open: en, Q, clk, clr
  Multiplexer #(.width(32)) multiplexer_3 (.out(multiplexer_3_out));  // open: in0, in1, sel, en
  Register #(.width(32)) t8 (.D(multiplexer_4_out));  // open: en, Q, clk, clr
  Multiplexer #(.width(32)) multiplexer_4 (.out(multiplexer_4_out));  // open: in0, in1, sel, en
  Multiplexer #(.width(32)) multiplexer_5 (.out(multiplexer_5_out));  // open: in0, in1, sel, en
  Multiplexer #(.width(32)) multiplexer_6 (.out(multiplexer_6_out));  // open: in0, in1, sel, en
  Multiplexer #(.width(32)) multiplexer_7 (.out(multiplexer_7_out));  // open: in0, in1, sel, en
  Multiplexer #(.width(32)) multiplexer_8 (.out(multiplexer_8_out));  // open: in0, in1, sel, en
  Register #(.width(32)) at (.D(multiplexer_5_out));  // open: en, Q, clk, clr
  Register #(.width(32)) t1 (.D(multiplexer_6_out));  // open: en, Q, clk, clr
  Register #(.width(32)) s1 (.D(multiplexer_7_out));  // open: en, Q, clk, clr
  Register #(.width(32)) t9 (.D(multiplexer_8_out));  // open: en, Q, clk, clr
  Multiplexer #(.width(32)) multiplexer_9 (.out(multiplexer_9_out));  // open: in0, in1, sel, en
  Register #(.width(32)) v0 (.D(multiplexer_9_out));  // open: en, Q, clk, clr
  Register #(.width(32)) t2 (.D(multiplexer_10_out));  // open: en, Q, clk, clr
  Multiplexer #(.width(32)) multiplexer_10 (.out(multiplexer_10_out));  // open: in0, in1, sel, en
  Register #(.width(32)) s2 (.D(multiplexer_11_out));  // open: en, Q, clk, clr
  Multiplexer #(.width(32)) multiplexer_11 (.out(multiplexer_11_out));  // open: in0, in1, sel, en
  Multiplexer #(.width(32)) multiplexer_12 (.out(multiplexer_12_out));  // open: in0, in1, sel, en
  Register #(.width(32)) k0 (.D(multiplexer_12_out));  // open: en, Q, clk, clr
  Multiplexer #(.width(32)) multiplexer_13 (.out(multiplexer_13_out));  // open: in0, in1, sel, en
  Register #(.width(32)) v1 (.D(multiplexer_13_out));  // open: en, Q, clk, clr
  Register #(.width(32)) t3 (.D(multiplexer_14_out));  // open: en, Q, clk, clr
  Multiplexer #(.width(32)) multiplexer_14 (.out(multiplexer_14_out));  // open: in0, in1, sel, en
  Register #(.width(32)) s3 (.D(multiplexer_15_out));  // open: en, Q, clk, clr
  Multiplexer #(.width(32)) multiplexer_15 (.out(multiplexer_15_out));  // open: in0, in1, sel, en
  Register #(.width(32)) k1 (.D(multiplexer_16_out));  // open: en, Q, clk, clr
  Multiplexer #(.width(32)) multiplexer_16 (.out(multiplexer_16_out));  // open: in0, in1, sel, en
  Multiplexer #(.width(32)) multiplexer_17 (.out(multiplexer_17_out));  // open: in0, in1, sel, en
  Multiplexer #(.width(32)) multiplexer_18 (.out(multiplexer_18_out));  // open: in0, in1, sel, en
  Multiplexer #(.width(32)) multiplexer_19 (.out(multiplexer_19_out));  // open: in0, in1, sel, en
  Multiplexer #(.width(32)) multiplexer_20 (.out(multiplexer_20_out));  // open: in0, in1, sel, en
  Register #(.width(32)) a0 (.D(multiplexer_17_out));  // open: en, Q, clk, clr
  Register #(.width(32)) t4 (.D(multiplexer_18_out));  // open: en, Q, clk, clr
  Register #(.width(32)) s4 (.D(multiplexer_19_out));  // open: en, Q, clk, clr
  Register #(.width(32)) gp (.D(multiplexer_20_out));  // open: en, Q, clk, clr
  Multiplexer #(.width(32)) multiplexer_21 (.out(multiplexer_21_out));  // open: in0, in1, sel, en
  Register #(.width(32)) a1 (.D(multiplexer_21_out));  // open: en, Q, clk, clr
  Register #(.width(32)) t5 (.D(multiplexer_22_out));  // open: en, Q, clk, clr
  Multiplexer #(.width(32)) multiplexer_22 (.out(multiplexer_22_out));  // open: in0, in1, sel, en
  Register #(.width(32)) s5 (.D(multiplexer_23_out));  // open: en, Q, clk, clr
  Multiplexer #(.width(32)) multiplexer_23 (.out(multiplexer_23_out));  // open: in0, in1, sel, en
  Register #(.width(32)) sp (.D(multiplexer_24_out));  // open: en, Q, clk, clr
  Multiplexer #(.width(32)) multiplexer_24 (.out(multiplexer_24_out));  // open: in0, in1, sel, en
  Multiplexer #(.width(32)) multiplexer_25 (.out(multiplexer_25_out));  // open: in0, in1, sel, en
  Multiplexer #(.width(32)) multiplexer_26 (.out(multiplexer_26_out));  // open: in0, in1, sel, en
  Multiplexer #(.width(32)) multiplexer_27 (.out(multiplexer_27_out));  // open: in0, in1, sel, en
  Multiplexer #(.width(32)) multiplexer_28 (.out(multiplexer_28_out));  // open: in0, in1, sel, en
  Register #(.width(32)) a2 (.D(multiplexer_25_out));  // open: en, Q, clk, clr
  Register #(.width(32)) t6 (.D(multiplexer_26_out));  // open: en, Q, clk, clr
  Register #(.width(32)) s6 (.D(multiplexer_27_out));  // open: en, Q, clk, clr
  Register #(.width(32)) fp (.D(multiplexer_28_out));  // open: en, Q, clk, clr
  Multiplexer #(.width(32)) multiplexer_29 (.out(multiplexer_29_out));  // open: in0, in1, sel, en
  Multiplexer #(.width(32)) multiplexer_30 (.out(multiplexer_30_out));  // open: in0, in1, sel, en
  Multiplexer #(.width(32)) multiplexer_31 (.out(multiplexer_31_out));  // open: in0, in1, sel, en
  Multiplexer #(.width(32)) multiplexer_32 (.out(multiplexer_32_out));  // open: in0, in1, sel, en
  Register #(.width(32)) a3 (.D(multiplexer_29_out));  // open: en, Q, clk, clr
  Register #(.width(32)) t7 (.D(multiplexer_30_out));  // open: en, Q, clk, clr
  Register #(.width(32)) s7 (.D(multiplexer_31_out));  // open: en, Q, clk, clr
  Register #(.width(32)) ra (.D(multiplexer_32_out));  // open: en, Q, clk, clr
endmodule
