// Logisim project cpu.circ as structural Verilog: 4 circuits, main circuit main
module main (
  input  [31:0] INSTRUCTION,
  input  CLOCK,
  output [31:0] FETCH_ADDRESS,
  output [31:0] s0_Value,
  output [31:0] s1_Value,
  output [31:0] s2_Value,
  output [31:0] ra_Value,
  output [31:0] sp_Value,
  output Overflow
);

  wire add, addi, addiu, addu, \and , and_1_out, and_2_out, andi, beq, bne, clz, comparator_2_eq,
       comparator_3_eq, comparator_4_eq, comparator_5_eq, comparator_6_eq, comparator_7_eq, comparator_8_eq,
       comparator_9_eq, comparator_10_eq, comparator_11_eq, comparator_12_eq, comparator_28_eq,
       comparator_29_eq, comparator_30_eq, comparator_31_eq, comparator_32_eq, comparator_33_eq,
       comparator_34_eq, comparator_35_eq, comparator_36_eq, comparator_37_eq, equal, is_iType, is_Jtype,
       IsRType, j, jal, jr, lui, lw, not_1_out, \or , or_1_out, or_3_out, or_4_out, or_6_out, or_8_out, ori,
       ShiftType, sign, sll, slt, slti, sltiu, sltu, sra, srl, sw, write_enable;
  wire [3:0] multiplexer_8_out, SwitchL, SwitchR;
  wire [4:0] multiplexer_4_out, multiplexer_5_out;
  wire [31:0] adder_2_out, adder_3_out, bit_extender_1_out, bit_extender_2_out, clz_circ_1_output, FA_4, Imm,
       main_2_result, MemData, multiplexer_1_out, multiplexer_2_out, multiplexer_3_out, multiplexer_6_out,
       multiplexer_7_out, multiplexer_10_out, multiplexer_11_out, multiplexer_12_out, R_rs, R_rt, Shamt,
       shifter_1_out, shifter_2_out, WriteData;

  Comparator #(.width(32)) comparator_1 (.a(R_rs), .b(R_rt), .eq(equal));  // open: gt, lt
  Adder #(.width(32)) adder_1 (.a(32'h4), .b(FETCH_ADDRESS), .out(FA_4));  // open: cin, cout
  not not_1 (not_1_out, equal);
  Comparator #(.width(6)) comparator_2 (.a(INSTRUCTION[31:26]), .b(6'b001000), .eq(comparator_2_eq));  // open: gt, lt
  Comparator #(.width(6)) comparator_3 (.a(INSTRUCTION[31:26]), .b(6'b001001), .eq(comparator_3_eq));  // open: gt, lt
  Comparator #(.width(6)) comparator_4 (.a(INSTRUCTION[31:26]), .b(6'b001100), .eq(comparator_4_eq));  // open: gt, lt
  Comparator #(.width(6)) comparator_5 (.a(INSTRUCTION[31:26]), .b(6'b000100), .eq(comparator_5_eq));  // open: gt, lt
  Comparator #(.width(6)) comparator_6 (.a(INSTRUCTION[31:26]), .b(6'b000101), .eq(comparator_6_eq));  // open: gt, lt
  Comparator #(.width(6)) comparator_7 (.a(INSTRUCTION[31:26]), .b(6'b001111), .eq(comparator_7_eq));  // open: gt, lt
  Comparator #(.width(6)) comparator_8 (.a(INSTRUCTION[31:26]), .b(6'b100011), .eq(comparator_8_eq));  // open: gt, lt
  Comparator #(.width(6)) comparator_9 (.a(INSTRUCTION[31:26]), .b(6'b001101), .eq(comparator_9_eq));  // open: gt, lt
  Comparator #(.width(6)) comparator_10 (.a(INSTRUCTION[31:26]), .b(6'b101011), .eq(comparator_10_eq));  // open: gt, lt
  Comparator #(.width(6)) comparator_11 (.a(INSTRUCTION[31:26]), .b(6'b001010), .eq(comparator_11_eq));  // open: gt, lt
  Comparator #(.width(6)) comparator_12 (.a(INSTRUCTION[31:26]), .b(6'b001011), .eq(comparator_12_eq));  // open: gt, lt
  Adder #(.width(32)) adder_2 (.a(FA_4), .b(shifter_1_out), .out(adder_2_out));  // open: cin, cout
  Shifter #(.width(32)) shifter_1 (.in(Imm), .\dist (5'b00010), .out(shifter_1_out));
  and and_1 (and_1_out, beq, equal);
  or or_1 (or_1_out, and_1_out, and_2_out);
  and and_2 (and_2_out, not_1_out, bne);
  or or_2 (is_Jtype, jal, j);
  Comparator #(.width(6)) comparator_13 (.a(INSTRUCTION[31:26]), .b({6{1'b0}}), .eq(IsRType));  // open: gt, lt
  Comparator #(.width(6)) comparator_14 (.a(INSTRUCTION[31:26]), .b(6'b000010), .eq(j));  // open: gt, lt
  Comparator #(.width(6)) comparator_15 (.a(INSTRUCTION[31:26]), .b(6'b000011), .eq(jal));  // open: gt, lt
  Comparator #(.width(6)) comparator_16 (.a(INSTRUCTION[31:26]), .b(6'b000100), .eq(beq));  // open: gt, lt
  Comparator #(.width(6)) comparator_17 (.a(INSTRUCTION[31:26]), .b(6'b000101), .eq(bne));  // open: gt, lt
  Comparator #(.width(6)) comparator_18 (.a(INSTRUCTION[31:26]), .b(6'b001001), .eq(addiu));  // open: gt, lt
  Comparator #(.width(6)) comparator_19 (.a(INSTRUCTION[31:26]), .b(6'b001100), .eq(andi));  // open: gt, lt
  Comparator #(.width(6)) comparator_20 (.a(INSTRUCTION[31:26]), .b(6'b001101), .eq(ori));  // open: gt, lt
  Comparator #(.width(6)) comparator_21 (.a(INSTRUCTION[31:26]), .b(6'b001011), .eq(sltiu));  // open: gt, lt
  Comparator #(.width(6)) comparator_22 (.a(INSTRUCTION[31:26]), .b(6'b001000), .eq(addi));  // open: gt, lt
  Comparator #(.width(6)) comparator_23 (.a(INSTRUCTION[31:26]), .b(6'b001010), .eq(slti));  // open: gt, lt
  Comparator #(.width(6)) comparator_24 (.a(INSTRUCTION[31:26]), .b(6'b001111), .eq(lui));  // open: gt, lt
  Comparator #(.width(6)) comparator_25 (.a(INSTRUCTION[31:26]), .b(6'b110101), .eq(lw));  // open: gt, lt
  Comparator #(.width(6)) comparator_26 (.a(INSTRUCTION[31:26]), .b(6'b101011), .eq(sw));  // open: gt, lt
  Comparator #(.width(6)) comparator_27 (.a(INSTRUCTION[31:26]), .b(6'b011100), .eq(clz));  // open: gt, lt
  Multiplexer #(.width(32)) multiplexer_1 (
    .in0(FA_4), .in1(adder_2_out), .out(multiplexer_1_out), .sel(or_1_out));  // open: en
  Multiplexer #(.width(32)) multiplexer_2 (
    .in0(multiplexer_1_out), .in1({FA_4[31:28], INSTRUCTION[25:0], 2'b00}), .out(multiplexer_2_out),
    .sel(or_3_out));  // open: en
  or or_3 (or_3_out, jal, j);
  Multiplexer #(.width(32)) multiplexer_3 (
    .in0(multiplexer_2_out), .in1(R_rs), .out(multiplexer_3_out), .sel(jr));  // open: en
  or or_4 (or_4_out, beq, bne, j, jr);
  not not_2 (write_enable, or_4_out);
  Comparator #(.width(6)) comparator_28 (.a({6{1'b0}}), .b(INSTRUCTION[5:0]), .eq(comparator_28_eq));  // open: gt, lt
  Comparator #(.width(6)) comparator_29 (.a(6'b000010), .b(INSTRUCTION[5:0]), .eq(comparator_29_eq));  // open: gt, lt
  Comparator #(.width(6)) comparator_30 (.a(6'b000011), .b(INSTRUCTION[5:0]), .eq(comparator_30_eq));  // open: gt, lt
  Comparator #(.width(6)) comparator_31 (.a(INSTRUCTION[5:0]), .b(6'b001000), .eq(comparator_31_eq));  // open: gt, lt
  Comparator #(.width(6)) comparator_32 (.a(INSTRUCTION[5:0]), .b(6'b100000), .eq(comparator_32_eq));  // open: gt, lt
  Comparator #(.width(6)) comparator_33 (.a(INSTRUCTION[5:0]), .b(6'b100001), .eq(comparator_33_eq));  // open: gt, lt
  Comparator #(.width(6)) comparator_34 (.a(INSTRUCTION[5:0]), .b(6'b100100), .eq(comparator_34_eq));  // open: gt, lt
  Comparator #(.width(6)) comparator_35 (.a(INSTRUCTION[5:0]), .b(6'b100101), .eq(comparator_35_eq));  // open: gt, lt
  Comparator #(.width(6)) comparator_36 (.a(INSTRUCTION[5:0]), .b(6'b101010), .eq(comparator_36_eq));  // open: gt, lt
  Comparator #(.width(6)) comparator_37 (.a(INSTRUCTION[5:0]), .b(6'b101011), .eq(comparator_37_eq));  // open: gt, lt
  Register #(.width(32)) PC (.D(multiplexer_3_out), .Q(FETCH_ADDRESS), .clk(CLOCK));  // open: en, clr
  Multiplexer #(.width(5)) multiplexer_4 (
    .in0(INSTRUCTION[20:16]), .in1(INSTRUCTION[15:11]), .out(multiplexer_4_out), .sel(IsRType));  // open: en
  or or_5 (is_iType, comparator_12_eq, comparator_2_eq, comparator_3_eq, comparator_4_eq, comparator_5_eq, comparator_6_eq, comparator_7_eq, comparator_8_eq, comparator_9_eq, comparator_10_eq, comparator_11_eq);
  Multiplexer #(.width(5)) multiplexer_5 (
    .in0(multiplexer_4_out), .in1({5{1'b1}}), .out(multiplexer_5_out), .sel(jal));  // open: en
  and and_3 (sll, IsRType, comparator_28_eq);
  and and_4 (srl, IsRType, comparator_29_eq);
  and and_5 (sra, IsRType, comparator_30_eq);
  and and_6 (jr, IsRType, comparator_31_eq);
  and and_7 (add, IsRType, comparator_32_eq);
  and and_8 (addu, IsRType, comparator_33_eq);
  and and_9 (\and , IsRType, comparator_34_eq);
  and and_10 (\or , IsRType, comparator_35_eq);
  and and_11 (slt, IsRType, comparator_36_eq);
  and and_12 (sltu, IsRType, comparator_37_eq);
  or or_6 (or_6_out, beq, bne);
  or or_7 (ShiftType, sll, srl, sra);
  regfile_main main_1 (
    .Read_Register_1(INSTRUCTION[25:21]), .Read_Register_2(INSTRUCTION[20:16]),
    .Write_Register(multiplexer_5_out), .Write_Data(WriteData), .Write_Enable(write_enable), .Clock(CLOCK),
    .Read_Data_1(R_rs), .Read_Data_2(R_rt), .s0_Value(s0_Value), .s1_Value(s1_Value), .s2_Value(s2_Value),
    .ra_Value(ra_Value), .sp_Value(sp_Value));
  Multiplexer #(.width(32)) multiplexer_6 (.in0(Imm), .in1(R_rt), .out(multiplexer_6_out), .sel(or_8_out));  // open: en
  or or_8 (or_8_out, IsRType, or_6_out);
  Multiplexer #(.width(32)) multiplexer_7 (
    .in0(R_rs), .in1(Shamt), .out(multiplexer_7_out), .sel(ShiftType));  // open: en
  assign bit_extender_1_out = {{16{1'b0}}, INSTRUCTION[15:0]};  // Bit_Extender bit_extender_1
  assign bit_extender_2_out = {{16{INSTRUCTION[15]}}, INSTRUCTION[15:0]};  // Bit_Extender bit_extender_2
  assign Shamt = {{27{INSTRUCTION[10]}}, INSTRUCTION[10:6]};  // Bit_Extender bit_extender_3
  Adder #(.width(32)) adder_3 (.a(R_rs), .b(Imm), .out(adder_3_out));  // open: cin, cout
  alu_main main_2 (
    .Switch(multiplexer_8_out), .X(multiplexer_7_out), .Equal(equal), .Result(main_2_result),
    .Signed_Overflow(Overflow), .Y(multiplexer_6_out));
  Multiplexer #(.width(4)) multiplexer_8 (
    .in0(SwitchL), .in1(SwitchR), .out(multiplexer_8_out), .sel(IsRType));  // open: en
  Multiplexer #(.width(32)) multiplexer_9 (
    .in0(bit_extender_1_out), .in1(bit_extender_2_out), .out(Imm), .sel(sign));  // open: en
  // mem_main main_3: pin names not known; wires that end beside it: adder_3_out, R_rt, sw, CLOCK, MemData
  Multiplexer #(.width(32)) multiplexer_10 (
    .in0(main_2_result), .in1(MemData), .out(multiplexer_10_out), .sel(lw));  // open: en
  L_Switch_Control l_switch_control_1 (
    .a(INSTRUCTION[31]), .b(INSTRUCTION[30]), .c(INSTRUCTION[29]), .d(INSTRUCTION[28]), .e(INSTRUCTION[27]),
    .f(INSTRUCTION[26]), .s0(SwitchL[3]), .s1(SwitchL[2]), .s2(SwitchL[1]), .s3(SwitchL[0]));  // open: MemWrite, MemToReg
  R_Switch_Control r_switch_control_1 (
    .a(INSTRUCTION[5]), .b(INSTRUCTION[4]), .c(INSTRUCTION[3]), .d(INSTRUCTION[2]), .e(INSTRUCTION[1]),
    .f(INSTRUCTION[0]), .s0(SwitchR[3]), .s1(SwitchR[2]), .s2(SwitchR[1]), .s3(SwitchR[0]));  // open: RTypeRR1
  or or_9 (sign, addi, andi, ori, slti);
  Multiplexer #(.width(32)) multiplexer_11 (
    .in0(multiplexer_10_out), .in1(FA_4), .out(multiplexer_11_out), .sel(jal));  // open: en
  Shifter #(.width(32)) shifter_2 (.in(Imm), .\dist (5'b10000), .out(shifter_2_out));
  Multiplexer #(.width(32)) multiplexer_12 (
    .in0(multiplexer_11_out), .in1(shifter_2_out), .out(multiplexer_12_out), .sel(lui));  // open: en
  clz_circ clz_circ_1 (.Input(R_rs), .Output(clz_circ_1_output));
  Multiplexer #(.width(32)) multiplexer_13 (
    .in0(multiplexer_12_out), .in1(clz_circ_1_output), .out(WriteData), .sel(clz));  // open: en

  // Other names for the same wires on the sheet: FunctType[5:0] = INSTRUCTION[5:0]; Imm1[15:0] = INSTRUCTION[15:0];
  //   JTypeAddress[25:0] = INSTRUCTION[25:0]; Shamt1[4:0] = INSTRUCTION[10:6]; rd[4:0] = INSTRUCTION[15:11];
  //   rt[4:0] = INSTRUCTION[20:16]; rs[4:0] = INSTRUCTION[25:21]; clk = CLOCK; fetch_addr[31:0] = FETCH_ADDRESS;
  //   Opcode[5:0] = INSTRUCTION[31:26]; ra[31:0] = ra_Value; s0[31:0] = s0_Value; s1[31:0] = s1_Value;
  //   s2[31:0] = s2_Value; sp[31:0] = sp_Value

  // Notes on the sheet:
  //   Output
  //   These are outputs/inputs from run.circ
  //   Splits up Instructions
  //   Checks if op i I type (addi, addiu, andi, beq, bne, lui, lw , ori, sw)
  //   Inputs
  //   These are DEBUG/TEST outputs from your circuit.
endmodule

module clz_circ (
  input  [31:0] Input,
  output [31:0] Output
);

  wire and_1_out, comparator_1_eq, comparator_2_eq;
  wire [4:0] bitfinder_1_index;
  wire [31:0] adder_1_out, subtractor_1_out;

  BitFinder #(.width(32), .\type ("high1")) bitfinder_1 (.in(Input), .index(bitfinder_1_index));  // open: found
  Adder #(.width(32)) adder_1 (.a({{27{1'b0}}, bitfinder_1_index}), .b(32'h1), .out(adder_1_out));  // open: cin, cout
  Subtractor #(.width(32)) subtractor_1 (.a(32'h20), .b(adder_1_out), .out(subtractor_1_out));  // open: bin, bout
  Comparator #(.width(32)) comparator_1 (.a(subtractor_1_out), .b(32'h1f), .eq(comparator_1_eq));  // open: gt, lt
  Comparator #(.width(32)) comparator_2 (.a(Input), .b({32{1'b0}}), .eq(comparator_2_eq));  // open: gt, lt
  and and_1 (and_1_out, comparator_1_eq, comparator_2_eq);
  Multiplexer #(.width(32)) multiplexer_1 (
    .in0(subtractor_1_out), .in1(32'h20), .out(Output), .sel(and_1_out));  // open: en

  // Other names for the same wires on the sheet: Initial_In[31:0] = Input
endmodule

module R_Switch_Control (
  input  a,
  input  b,
  input  c,
  input  d,
  input  e,
  input  f,
  output RTypeRR1,
  output s0,
  output s1,
  output s2,
  output s3
);

  wire and_1_out, and_2_out, and_3_out, and_4_out, and_5_out, and_6_out, and_7_out, and_8_out, and_9_out,
       not_1_out, not_2_out, not_3_out, not_4_out, not_5_out, not_6_out, not_7_out, not_8_out, not_9_out,
       not_10_out, not_11_out, not_12_out;

  not not_1 (not_1_out, b);
  not not_2 (not_2_out, d);
  not not_3 (not_3_out, e);
  not not_4 (not_4_out, f);
  not not_5 (not_5_out, d);
  not not_6 (not_6_out, e);
  not not_7 (not_7_out, f);
  not not_8 (not_8_out, f);
  not not_9 (not_9_out, c);
  not not_10 (not_10_out, f);
  not not_11 (not_11_out, c);
  not not_12 (not_12_out, f);
  and and_1 (and_1_out, not_1_out, c, not_2_out, not_3_out, not_4_out);
  and and_2 (and_2_out, d, f);
  and and_3 (and_3_out, not_5_out, not_6_out, f);
  and and_4 (and_4_out, d, not_7_out);
  and and_5 (and_5_out, e, f);
  and and_6 (and_6_out, a, not_8_out);
  and and_7 (and_7_out, not_9_out, e, not_10_out);
  and and_8 (and_8_out, c, f);
  and and_9 (and_9_out, a, not_11_out, not_12_out);
  or or_1 (RTypeRR1, and_1_out, a);
  or or_2 (s0, and_2_out, c);
  or or_3 (s1, and_3_out, and_4_out);
  or or_4 (s2, and_5_out, and_6_out);
  or or_5 (s3, and_7_out, and_8_out, and_9_out);

  // Notes on the sheet:
  //   We put this Not here
endmodule

module L_Switch_Control (
  input  a,
  input  b,
  input  c,
  input  d,
  input  e,
  input  f,
  output s0,
  output s1,
  output s2,
  output s3,
  output MemWrite,
  output MemToReg
);

  wire and_1_out, and_2_out, and_3_out, and_4_out, and_5_out, and_6_out, and_7_out, and_8_out, and_9_out,
       and_10_out, and_11_out, and_12_out, and_13_out, and_14_out, and_15_out, and_16_out, and_17_out,
       and_18_out, and_19_out, and_20_out, and_21_out, and_22_out, and_23_out, and_24_out, and_25_out,
       not_1_out, not_2_out, not_3_out, not_4_out, not_5_out, not_6_out, not_7_out, not_8_out, not_9_out,
       not_10_out, not_11_out, not_12_out, not_13_out, not_14_out, not_15_out, not_16_out, not_17_out,
       not_18_out, not_19_out, not_20_out;

  not not_1 (not_1_out, e);
  not not_2 (not_2_out, a);
  not not_3 (not_3_out, f);
  not not_4 (not_4_out, d);
  not not_5 (not_5_out, e);
  not not_6 (not_6_out, f);
  not not_7 (not_7_out, c);
  not not_8 (not_8_out, f);
  not not_9 (not_9_out, d);
  not not_10 (not_10_out, c);
  and and_1 (and_1_out, not_10_out, not_1_out);
  not not_11 (not_11_out, c);
  and and_2 (and_2_out, not_11_out, d);
  and and_3 (and_3_out, d, f);
  and and_4 (and_4_out, not_2_out, c, e);
  and and_5 (and_5_out, c, e, not_3_out);
  and and_6 (and_6_out, b, e);
  and and_7 (and_7_out, not_4_out, not_5_out, f);
  and and_8 (and_8_out, c, d, not_6_out);
  and and_9 (and_9_out, not_7_out, d, e);
  and and_10 (and_10_out, c, not_8_out);
  and and_11 (and_11_out, c, not_9_out, e);
  and and_12 (and_12_out, b, e);
  and and_13 (and_13_out, a, e);
  not not_12 (not_12_out, c);
  not not_13 (not_13_out, e);
  not not_14 (not_14_out, e);
  not not_15 (not_15_out, f);
  not not_16 (not_16_out, c);
  and and_14 (and_14_out, not_16_out, d);
  not not_17 (not_17_out, d);
  and and_15 (and_15_out, c, not_17_out, e, f);
  not not_18 (not_18_out, c);
  not not_19 (not_19_out, c);
  not not_20 (not_20_out, e);
  and and_16 (and_16_out, not_12_out, not_13_out);
  and and_17 (and_17_out, not_14_out, not_15_out);
  and and_18 (and_18_out, b, not_18_out);
  and and_19 (and_19_out, b, e, f);
  and and_20 (and_20_out, a, not_19_out);
  and and_21 (and_21_out, a, e, f);
  and and_22 (and_22_out, a, not_20_out);
  and and_23 (and_23_out, a, d);
  and and_24 (and_24_out, a, c);
  and and_25 (and_25_out, a, b);
  or or_1 (s0, and_1_out, and_2_out, and_3_out, and_4_out, and_5_out, and_6_out);
  or or_2 (s1, and_7_out, and_8_out);
  or or_3 (s2, and_9_out, and_10_out, and_11_out, and_12_out, and_13_out);
  or or_4 (s3, and_16_out, and_17_out, and_14_out, and_15_out, and_18_out, and_19_out, and_20_out, and_21_out);
  or or_5 (MemWrite, and_22_out, and_23_out, and_24_out, and_25_out);

  assign MemToReg = a;
endmodule
