// Logisim project func_test.circ as structural Verilog: 1 circuit, main circuit main
module main (
  output [31:0] s0_Value,
  output [31:0] s1_Value,
  output [31:0] s2_Value,
  output [31:0] sp_Value
);

  wire clock_1_out;
  wire [31:0] main_1_fetch_address, rom_1_data;

  Clock clock_1 (.out(clock_1_out));
  cpu_main main_1 (
    .INSTRUCTION(rom_1_data), .CLOCK(clock_1_out), .FETCH_ADDRESS(main_1_fetch_address), .s0_Value(s0_Value),
    .s1_Value(s1_Value), .s2_Value(s2_Value), .sp_Value(sp_Value));  // open: ra_Value, Overflow
  ROM #(.addrWidth(24), .dataWidth(32)) rom_1 (.addr(main_1_fetch_address[25:2]), .data(rom_1_data));  // open: sel

  // Notes on the sheet:
  //   YOUR CPU SHOULD FIT IN HERE!
  //   Instruction Memory
  //   contents of rom_1 (hex, n*v repeats v):
  //   341d0000 2008000c 1002020 c000006 404020 800000a 844820 1244820 91020 3e00008 35100000 37f10000
  //   20120001
endmodule
